# Fritzing sketch RTDSensingCircuit (saved by Fritzing 0.9.3b)
breadboards: 1

parts:
  R2 = Resistor [tolerance=±1% resistance=2k package="0402 [SMD]"]
  R3 = Resistor [tolerance=±1% resistance=100 package="0402 [SMD]"]
  R4 = Resistor [tolerance=±1% resistance=2k package="0402 [SMD]"]
  Rs = Resistor [tolerance=±0.1% resistance=5 package=THT]
  Vin = DC Power [voltage=12V]
  Instrumentation_Amplifier = AD623 - Instrumentation Amplifier [part_number=ad623]
  R7 = Resistor [tolerance=±5% resistance=2k package="0402 [SMD]"]
  R8 = Resistor [tolerance=±5% resistance=2k package="0402 [SMD]"]
  Rg = Resistor [tolerance=±1% resistance=2k package="0402 [SMD]"]
  part = Voltage Regulator - 5V [package="TO220 [THT]"]
  C1 = Tantalum Capacitor [capacitance="1 μF" package="D 7343 [SMD, tantalum]"]
  3-Wire_RTD = Temperature Sensor (Thermistor) [thermistor_type=NTC package=THT]
  Vout = Header 2 [package=molex-1x2_lock]
  Vreg = Header 2 [package=molex-1x2_lock]

nets:
  N1: R2.Pin_0, R4.Pin_1
  N2: R2.Pin_1, R7.Pin_0, 3-Wire_RTD.pin_1
  N3: R3.Pin_0, R4.Pin_0
  N4: R3.Pin_1, Rs.Pin_0, part.output_voltage, Vreg.1
  N5: Rs.Pin_1, 3-Wire_RTD.pin_0
  N6: Vin.V+, Instrumentation_Amplifier.+Vs
  GND: Vin.V-, Instrumentation_Amplifier.-Vs, Instrumentation_Amplifier.Ref, C1.-, Vout.2, Vreg.2
  N7: Instrumentation_Amplifier.-Rg, Rg.Pin_0
  N8: Instrumentation_Amplifier.-IN, R7.Pin_1
  N9: Instrumentation_Amplifier.+IN, R8.Pin_1
  N10: Instrumentation_Amplifier.Vout, Vout.1
  N11: Instrumentation_Amplifier.+Rg, Rg.Pin_1
