# Fritzing sketch RTDSensingCircuit2 (saved by Fritzing 0.9.3b)
breadboards: 1

parts:
  R2 = Resistor [tolerance=±1% resistance=2k package="0402 [SMD]"]
  R3 = Resistor [tolerance=±1% resistance=100 package="0402 [SMD]"]
  R4 = Resistor [tolerance=±1% resistance=2k package="0402 [SMD]"]
  Rs = Resistor [tolerance=±0.1% resistance=5 package=THT]
  V1 = DC Power [voltage=5]
  Single_and_Dual-Supply_Rail-to-Rail_Low_Cost_Instrumentation_Amplifier1 = AD623 - Instrumentation Amplifier [part_number=ad623]
  R7 = Resistor [tolerance=±5% resistance=2k package="0402 [SMD]"]
  R8 = Resistor [tolerance=±5% resistance=2k package="0402 [SMD]"]
  Rg = Resistor [tolerance=±1% resistance=2k package="0402 [SMD]"]
  U1 = Voltage Regulator - 5V [package="TO220 [THT]"]
  C1 = Tantalum Capacitor [capacitance="1 μF" package="D 7343 [SMD, tantalum]"]
  3-Wire_RTD = Temperature Sensor (Thermistor) [thermistor_type=NTC package=THT]
  JP1 = Header 2 [package=molex-1x2_lock]

nets:
  N1: R2.Pin_0, R4.Pin_1
  N2: R2.Pin_1, R7.Pin_0, 3-Wire_RTD.pin_1
  N3: R3.Pin_0, R4.Pin_0
  N4: R3.Pin_1, Rs.Pin_0, U1.output_voltage
  N5: Rs.Pin_1, 3-Wire_RTD.pin_0
  N6: V1.V+, Single_and_Dual-Supply_Rail-to-Rail_Low_Cost_Instrumentation_Amplifier1.+Vs
  GND: V1.V-, Single_and_Dual-Supply_Rail-to-Rail_Low_Cost_Instrumentation_Amplifier1.-Vs, Single_and_Dual-Supply_Rail-to-Rail_Low_Cost_Instrumentation_Amplifier1.Ref, C1.-, JP1.2
  N7: Single_and_Dual-Supply_Rail-to-Rail_Low_Cost_Instrumentation_Amplifier1.-Rg, Rg.Pin_0
  N8: Single_and_Dual-Supply_Rail-to-Rail_Low_Cost_Instrumentation_Amplifier1.-IN, R7.Pin_1
  N9: Single_and_Dual-Supply_Rail-to-Rail_Low_Cost_Instrumentation_Amplifier1.+IN, R8.Pin_1
  N10: Single_and_Dual-Supply_Rail-to-Rail_Low_Cost_Instrumentation_Amplifier1.Vout, JP1.1
  N11: Single_and_Dual-Supply_Rail-to-Rail_Low_Cost_Instrumentation_Amplifier1.+Rg, Rg.Pin_1
